// Logisim project Project2Given.circ as structural Verilog: 4 circuits, main circuit main
module main (
);

  wire and_1_out, and_2_out, B0, B1, B2, B3, B4, B5, B6, B7, B8, B9, BL, BU, C0, C1, C2, CLK, L1_l, L1_u,
       not_1_out, or_8_out, P1_v, R0, R1, R3, R4, Valid;
  wire [2:0] counter_1_q;
  wire [3:0] IB1_c0, P1_b0, register_2_q, register_3_q, register_4_q, register_5_q;

  Button n1 (.out(B1));
  Button n4 (.out(B4));
  Button n7 (.out(B7));
  Button L (.out(BL));
  Button n3 (.out(B3));
  Button n2 (.out(B2));
  Button n6 (.out(B6));
  Button n5 (.out(B5));
  Button n9 (.out(B9));
  Button n8 (.out(B8));
  Button U (.out(BU));
  Button n0 (.out(B0));
  or or_1 (R0, B3, B2, B1);
  or or_2 (R1, B6, B5, B4);
  or or_3 (R3, B9, B8, B7);
  or or_4 (R4, BU, B0, BL);
  or or_5 (C0, B1, B4, B7, BL);
  or or_6 (C1, B2, B5, B8, B0);
  or or_7 (C2, B3, B6, B9, BU);
  Clock clock_1 (.out(CLK));
  nand nand_1 (Valid, IB1_c0[0], IB1_c0[1], IB1_c0[2], IB1_c0[3]);
  // Probe on P1_b0
  Panel P1 (
    .R0(R0), .R1(R1), .R2(R3), .R3(R4), .C0(C0), .C1(C1), .C2(C2), .B0(P1_b0[0]), .B1(P1_b0[1]),
    .B2(P1_b0[2]), .B3(P1_b0[3]), .V(P1_v));
  LED Press (.in(P1_v));
  // Probe on IB1_c0
  InputBuffer IB1 (
    .B0(P1_b0[0]), .B1(P1_b0[1]), .B2(P1_b0[2]), .B3(P1_b0[3]), .V(P1_v), .CLK(not_1_out), .C0(IB1_c0[0]),
    .C1(IB1_c0[1]), .C2(IB1_c0[2]), .C3(IB1_c0[3]));
  not not_1 (not_1_out, CLK);
  Register #(.width(4)) register_1 (.D(register_2_q), .en(Valid), .clk(CLK));  // open: Q, clr
  Lock L1 (.C0(IB1_c0[0]), .C1(IB1_c0[1]), .C2(IB1_c0[2]), .C3(IB1_c0[3]), .CLK(CLK), .L(L1_l), .U(L1_u));
  Counter #(.max('h7), .width(3)) counter_1 (
    .count(or_8_out), .Q(counter_1_q), .up(L1_u), .clk(CLK));  // open: load, D, carry, clr
  or or_8 (or_8_out, L1_l, L1_u);
  Register #(.width(4)) register_2 (.D(register_3_q), .en(Valid), .clk(CLK), .Q(register_2_q));  // open: clr
  LED Unlocked (.in(and_1_out));
  and and_1 (and_1_out, ~counter_1_q[0], ~counter_1_q[1], ~counter_1_q[2]);  // AND_Gate
  Register #(.width(4)) register_3 (.D(register_4_q), .en(Valid), .clk(CLK), .Q(register_3_q));  // open: clr
  LED Locked (.in(and_2_out));
  and and_2 (and_2_out, ~counter_1_q[0], ~counter_1_q[1], counter_1_q[2]);  // AND_Gate
  Register #(.width(4)) register_4 (.D(register_5_q), .en(Valid), .clk(CLK), .Q(register_4_q));  // open: clr
  Register #(.width(4)) register_5 (.D(IB1_c0), .en(Valid), .clk(CLK), .Q(register_5_q));  // open: clr
endmodule

module Panel (
  input  R0,
  input  R1,
  input  R2,
  input  R3,
  input  C0,
  input  C1,
  input  C2,
  output B0,
  output B1,
  output B2,
  output B3,
  output V
);

  wire BUT0, BUT1, BUT2, BUT3, BUT4, BUT5, BUT6, BUT7, BUT8, BUT9, BUTL, BUTU, CV, RV;

  ExactlyOne xor_1 (.out(RV), .in0(R0), .in1(R1), .in2(R2), .in3(R3));
  ExactlyOne xor_2 (.out(CV), .in0(C0), .in1(C1), .in2(C2));
  and and_1 (V, RV, CV);
  and and_2 (BUT1, R0, C0);
  and and_3 (BUT2, R0, C1);
  and and_4 (BUT3, R0, C2);
  and and_5 (BUT4, R1, C0);
  and and_6 (BUT5, R1, C1);
  and and_7 (BUT6, R1, C2);
  and and_8 (BUT7, R2, C0);
  and and_9 (BUT8, R2, C1);
  and and_10 (BUT9, R2, C2);
  or or_1 (B0, BUT1, BUT3, BUT5, BUT7, BUT9, BUTU);
  or or_2 (B1, BUT2, BUT3, BUT6, BUT7, BUTL, BUTU);
  or or_3 (B2, BUT4, BUT5, BUT6, BUT7);
  or or_4 (B3, BUT8, BUT9, BUTL, BUTU);
  and and_11 (BUTL, R3, C0);
  and and_12 (BUT0, R3, C1);
  and and_13 (BUTU, R3, C2);

  // Notes on the sheet:
  //   Valid Row
  //   Valid Column
endmodule

module InputBuffer (
  input  B0,
  input  B1,
  input  B2,
  input  B3,
  input  V,
  input  CLK,
  output C0,
  output C1,
  output C2,
  output C3
);

  wire clock_1_out, multiplexer_1_out, register_1_q, undriven;

  Clock clock_1 (.out(clock_1_out));
  Register #(.width(1)) register_1 (.D(B0), .en(undriven), .clk(clock_1_out), .Q(register_1_q));  // open: clr
  Register #(.width(2)) register_2 (.clk(CLK));  // open: D, en, Q, clr
  Multiplexer multiplexer_1 (.in0(1'b0), .in1(register_1_q), .out(multiplexer_1_out));  // open: sel
endmodule

module Lock (
  input  C0,
  input  C1,
  input  C2,
  input  C3,
  input  CLK,
  output L,
  output U
);
endmodule
